# Fritzing sketch LED4_3 (saved by Fritzing 0.8.7b)
circuit board: 6.88566cm x 5.36311cm
breadboards: 1

parts:
  Part1 = Arduino Uno (Rev3)
  LED1 = LED - 5mm [color="Red (633nm)" package="5 mm [THT]"]
  LED2 = LED - 5mm [color="Red (633nm)" package="5 mm [THT]"]
  LED3 = LED - 5mm [color="Red (633nm)" package="5 mm [THT]"]
  LED4 = LED - 5mm [color="Red (633nm)" package="5 mm [THT]"]
  LED5 = LED - 5mm [color="Red (633nm)" package="5 mm [THT]"]
  LED6 = LED - 5mm [color="Red (633nm)" package="5 mm [THT]"]
  LED7 = LED - 5mm [color="Red (633nm)" package="5 mm [THT]"]
  LED8 = LED - 5mm [color="Red (633nm)" package="5 mm [THT]"]
  LED9 = LED - 5mm [color="Red (633nm)" package="5 mm [THT]"]
  LED10 = LED - 5mm [color="Red (633nm)" package="5 mm [THT]"]
  LED11 = LED - 5mm [color="Red (633nm)" package="5 mm [THT]"]
  LED12 = LED - 5mm [color="Red (633nm)" package="5 mm [THT]"]

nets:
  N1: Part1.D8, LED7.anode
  N2: Part1.D9_PWM, LED8.anode
  N3: Part1.D10_PWM/SS, LED9.anode
  N4: Part1.D11_PWM/MOSI, LED10.anode
  N5: Part1.D12/MISO, LED11.anode
  N6: Part1.D13/SCK, LED12.anode
  N7: Part1.D2, LED3.anode
  N8: Part1.D3_PWM, LED2.anode
  N9: Part1.D4, LED1.anode
  N10: Part1.D5_PWM, LED4.anode
  N11: Part1.D6_PWM, LED5.anode
  N12: Part1.D7, LED6.anode
  N13: LED1.cathode, LED2.cathode, LED3.cathode, LED4.cathode, LED5.cathode, LED6.cathode, LED7.cathode, LED8.cathode, LED9.cathode, LED10.cathode, LED11.cathode, LED12.cathode
